# Fritzing sketch SolderingIron (saved by Fritzing 0.9.3b)
breadboards: 1

parts:
  Часть1 = Arduino Pro Mini v13
  U1 = LM358 [package=dip08]
  S1 = Round Pushbutton
  RE1 = Rotary Encoder [package=THT]
  U5 = 7-SEGMENT-DISPLAY [package=7-segment-display]
  R1 = Resistor [tolerance=±5% resistance=220 package=THT]
  R2 = Resistor [tolerance=±5% resistance=220 package=THT]
  R3 = Resistor [tolerance=±5% resistance=220 package=THT]
  R4 = Resistor [tolerance=±5% resistance=220 package=THT]
  R5 = Resistor [tolerance=±5% resistance=220 package=THT]
  R6 = Resistor [tolerance=±5% resistance=220 package=THT]
  R7 = Resistor [tolerance=±5% resistance=220 package=THT]
  R8 = Resistor [tolerance=±5% resistance=10k package=THT]
  R9 = Resistor [tolerance=±5% resistance=10k package=THT]
  R10 = Resistor [tolerance=±5% resistance=10k package=THT]
  LED1 = LED - 5mm [color="Yellow (595nm)" package="5 mm [THT]"]
  R11 = Resistor [tolerance=±5% resistance=220 package=THT]
  Q1 = Basic FET P-Channel [package="TO220 [THT]"]
  DIN1 = DIN-5 jack (MIDI) [package=THT]
  R12 = Resistor [tolerance=±5% resistance=10 package=THT]
  R13 = Resistor [tolerance=±5% resistance=10k package=THT]
  R14 = Resistor [tolerance=±5% resistance=10k package=THT]
  S3 = Pushbutton [part_number=Encoder package=THT]
  R15 = Resistor [tolerance=±5% resistance=10k part_number=Termistor package=THT]
  S4 = Round Pushbutton
  R16 = Resistor [tolerance=±5% resistance=10k package=THT]
  R17 = Resistor [tolerance=±5% resistance=10k package=THT]

nets:
  5V: Часть1.VCC, U1.G$1_V+, R8.Pin_1, R9.Pin_1, R10.Pin_1, R15.Pin_1, R16.Pin_0, R17.Pin_1
  N1: Часть1.A4, S1.leg1, R16.Pin_1
  N2: Часть1.A5, S4.leg1, R17.Pin_0
  GND: Часть1.GND, U1.G$1_V-, S1.leg0, RE1.EncoderPinC, LED1.cathode, Q1.source, DIN1.5, R12.Pin_0, R14.Pin_0, S3.leg0, S4.leg0
  N3: Часть1.A3, U1.G$1_OUT, R13.Pin_1
  N4: Часть1.A2, R10.Pin_0, S3.leg1
  N5: Часть1.A1, RE1.EncoderPinA, R8.Pin_0
  N6: Часть1.A0, RE1.EncoderPinB, R9.Pin_0
  3D 7-seg pin 8?: Часть1.D13/SCK
  N7: Часть1.D12/MISO, U5.G2
  N8: Часть1.D11_PWM/MOSI, U5.G1
  N9: Часть1.D10_PWM/SS, R11.Pin_1
  N10: Часть1.D9_PWM, R5.Pin_0
  N11: Часть1.D8, R4.Pin_0
  N12: Часть1.D6_PWM, R3.Pin_0
  N13: Часть1.D5_PWM, R7.Pin_0
  N14: Часть1.D4, R2.Pin_0
  N15: Часть1.D3_PWM, R6.Pin_0
  N16: Часть1.D2, R1.Pin_0
  N17: U1.G$1_-IN, R12.Pin_1, R13.Pin_0
  N18: U1.G$1_+IN, DIN1.3
  N19: U5.E, R5.Pin_1
  N20: U5.D, R4.Pin_1
  N21: U5.C, R3.Pin_1
  N22: U5.B, R2.Pin_1
  N23: U5.A, R1.Pin_1
  N24: U5.F, R6.Pin_1
  N25: U5.G, R7.Pin_1
  N26: LED1.anode, R11.Pin_0
  N27: Q1.drain, DIN1.1
  +24V: DIN1.4
  A7: R14.Pin_1, R15.Pin_0

notes:
  A - 11, B - 7, C - 4, D - 2, E - 1, F - 10, G - 5, DP - 3, D1 - 12, D2 - 9, D3 - 8
